# Fritzing sketch ft232h_espnow_sketch (saved by Fritzing 0.9.10b)
breadboards: 2

parts:
  Part1 = Adafruit FT232H Breakout - USB C and STEMMA QT [part_number="Adafruit #2264"]
  A1 = ESP32-S3 zero  # not connected
  Part2 = Adafruit QT Py ESP32-S2 [part_number="Adafruit #5325"]  # not connected
  OLED1 = OLED 128x64 I2C Monochrome Display

nets:
  GND: Part1.GND, OLED1.GND
  +3V3: Part1.+3V3, OLED1.VDD
  N1: Part1.D1/SDA/MOSI, OLED1.SCK
  N2: Part1.D0/SCL/SCK, OLED1.SDA

custom parts:
  Adafruit FT232H Breakout - USB C and STEMMA QT: Wouldn't it be cool to drive a tiny OLED display, read a color sensor, or even just flash some LEDs directly from your computer? Sure you can program an Arduino or Trinket to talk to these devices and your computer, but why can't your computer just talk to those devices and sensors itself? Well, now your computer can talk to devices using the Adafruit FT232H breakout board! What can the FT232H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
  ESP32-S3 zero: ESP32-S3 Mini Development Board, Based on ESP32-S3FH4R2 Dual-Core Processor, 240MHz Running Frequency, 2.4GHz Wi-Fi & Bluetooth 5.
  Adafruit QT Py ESP32-S2: What has your favorite Espressif WiFi microcontroller, comes with our favorite connector - the STEMMA QT, a chainable I2C port, and has lots of Flash and RAM memory for your next IoT project? What will make your next IoT project flyyyyy? What a cutie pie! Or is it... a QT Py? This diminutive dev board comes with one of our new favorite lil chips, the ESP32-S2! The ESP32-S2 is a highly-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
